// Logisim project CAMILOYWALDO.circ as structural Verilog: 6 circuits, main circuit main
module main (
);

  wire and_1_out, and_2_out, and_3_out, AVAILABLE, CICLOROMCHECK, CLK, CLKRAM, comparator_1_eq,
       LECTURACOMPLETARAM, MOSTRARMENSAJE, not_1_out, not_2_out, not_3_out, not_4_out, or_1_out, or_2_out,
       RESETDIRECCIONRAM, RESETDIRECCIONROM;
  wire [2:0] BUSBOTONES, contador5_1_out_4;
  wire [6:0] POSICIONRAM, register_1_q, rom_1_data, SALIDARAM, TAMANIOMENSAJE;
  wire [9:0] BUSTECLADO, direccionrom_1_out_3;
  wire [41:0] D05, D11, D17, D23, D29, D35, D41, D47, D53, D59;

  not not_1 (not_1_out, AVAILABLE);
  and and_1 (and_1_out, not_1_out, MOSTRARMENSAJE);
  or or_1 (or_1_out, AVAILABLE, RESETDIRECCIONROM);
  not not_2 (not_2_out, BUSTECLADO[9]);
  and and_2 (and_2_out, not_1_out, CLK);
  Clock clock_1 (.out(CLK));
  or or_2 (or_2_out, RESETDIRECCIONRAM, not_2_out);
  Multiplexer multiplexer_1 (.in0(CICLOROMCHECK), .in1(CLK), .out(CLKRAM), .sel(AVAILABLE));
  or or_3 (RESETDIRECCIONRAM, BUSBOTONES[2], LECTURACOMPLETARAM, BUSBOTONES[0]);
  CONTADOR5 contador5_1 (
    .CLK(and_2_out), .X(and_1_out), .RESET(or_1_out), .out_4(contador5_1_out_4), .Z(CICLOROMCHECK));
  Keyboard keyboard_1 (.clk(CLK), .re(BUSTECLADO[9]), .clr(BUSBOTONES[2]), .avail(AVAILABLE), .data(BUSTECLADO[6:0]));
  and and_3 (and_3_out, BUSTECLADO[9], AVAILABLE);
  not not_3 (not_3_out, AVAILABLE);
  Button CARGARMENSAJE (.out(BUSBOTONES[1]));
  Button RESETBOTON (.out(BUSBOTONES[2]));
  DIRECCIONRAM direccionram_1 (.RESET(or_2_out), .CLK(CLKRAM), .out_3(POSICIONRAM));
  Button LEERMENSAJE (.out(BUSBOTONES[0]));
  D_Flip_Flop d_ff_1 (.D(1'b1), .clk(BUSBOTONES[1]), .Q(BUSTECLADO[9]), .reset(BUSBOTONES[2]));  // open: Qn, preset
  RAM #(.addrWidth(7), .clearpin("true"), .dataWidth(7)) ram_1 (
    .addr(POSICIONRAM), .we(and_3_out), .oe(not_3_out), .clk(CLKRAM), .din(BUSTECLADO[6:0]),
    .dout(SALIDARAM), .clr(BUSBOTONES[2]));
  or or_4 (RESETDIRECCIONROM, BUSBOTONES[2], BUSBOTONES[1], BUSBOTONES[0]);
  DIRECCIONROM direccionrom_1 (.DIN({3'b000, SALIDARAM}), .COUNT(contador5_1_out_4), .out_3(direccionrom_1_out_3));
  ROM #(.addrWidth(10), .dataWidth(7)) rom_1 (.addr(direccionrom_1_out_3), .data(rom_1_data));
  DotMatrix #(.matrixcols(60)) dotmatrix_1 (
    .col0(D59[41:35]), .col1(D59[34:28]), .col2(D59[27:21]), .col3(D59[20:14]), .col4(D59[13:7]),
    .col5(D59[6:0]), .col6(D53[41:35]), .col7(D53[34:28]), .col8(D53[27:21]), .col9(D53[20:14]),
    .col10(D53[13:7]), .col11(D53[6:0]), .col12(D47[41:35]), .col13(D47[34:28]), .col14(D47[27:21]),
    .col15(D47[20:14]), .col16(D47[13:7]), .col17(D47[6:0]), .col18(D41[41:35]), .col19(D41[34:28]),
    .col20(D41[27:21]), .col21(D41[20:14]), .col22(D41[13:7]), .col23(D41[6:0]), .col24(D35[41:35]),
    .col25(D35[34:28]), .col26(D35[27:21]), .col27(D35[20:14]), .col28(D35[13:7]), .col29(D35[6:0]),
    .col30(D29[41:35]), .col31(D29[34:28]), .col32(D29[27:21]), .col33(D29[20:14]), .col34(D29[13:7]),
    .col35(D29[6:0]), .col36(D23[41:35]), .col37(D23[34:28]), .col38(D23[27:21]), .col39(D23[20:14]),
    .col40(D23[13:7]), .col41(D23[6:0]), .col42(D17[41:35]), .col43(D17[34:28]), .col44(D17[27:21]),
    .col45(D17[20:14]), .col46(D17[13:7]), .col47(D17[6:0]), .col48(D11[41:35]), .col49(D11[34:28]),
    .col50(D11[27:21]), .col51(D11[20:14]), .col52(D11[13:7]), .col53(D11[6:0]), .col54(D05[41:35]),
    .col55(D05[34:28]), .col56(D05[27:21]), .col57(D05[20:14]), .col58(D05[13:7]), .col59(D05[6:0]));
  D_Flip_Flop d_ff_2 (.D(1'b1), .clk(BUSBOTONES[0]), .Q(MOSTRARMENSAJE), .reset(BUSBOTONES[2]));  // open: Qn, preset
  Comparator #(.width(7)) comparator_1 (.a(POSICIONRAM), .b(TAMANIOMENSAJE), .eq(comparator_1_eq));  // open: gt, lt
  and and_4 (LECTURACOMPLETARAM, CICLOROMCHECK, comparator_1_eq);
  Register #(.width(7)) register_1 (
    .D(POSICIONRAM), .en(not_4_out), .clk(CLKRAM), .Q(register_1_q), .clr(BUSBOTONES[2]));
  not not_4 (not_4_out, MOSTRARMENSAJE);
  COLREGISTROS colregistros_1 (
    .DIN(rom_1_data), .CLK(CLK), .RESET(BUSBOTONES[2]), .D05(D05), .D11(D11), .D17(D17), .D23(D23),
    .D29(D29), .D35(D35), .D41(D41), .D47(D47), .D53(D53), .D59(D59));
  Adder #(.width(7)) adder_1 (.a(register_1_q), .b(7'b0001010), .out(TAMANIOMENSAJE));  // open: cin, cout

  // Other names for the same wires on the sheet: LEERMENSAJE = BUSBOTONES[0]; CARGARMENSAJE = BUSBOTONES[1];
  //   BUSTECLADO[8:7] = {BUSBOTONES[2], AVAILABLE}; LIMPIARRAM = BUSBOTONES[2]; MASRESETS = BUSBOTONES[2];
  //   RESETBOTON = BUSBOTONES[2]; RESETTECLADO = BUSBOTONES[2]; DATATECLADO[6:0] = BUSTECLADO[6:0];
  //   LEERTECLADO = BUSTECLADO[9]

  // Notes on the sheet:
  //   contents of rom_1 (hex, n*v repeats v):
  //   8*0 7d 4*0 60 0 60 0 0 14 7f 14 7f 14 0 12 2a 7f 2a 24 0 1 26 8 32 40 0 2c 52 5a 24 a 0 0 0 60 4*0
  //   3e 41 5*0 41 3e 0 0 28 10 7c 10 28 0 8 8 3e 8 8 0 0 1 2 4*0 8 8 8 4*0 2 0 0 0 1 6 8 30 40 0 3e 45 49
  //   51 3e 0 11 21 7f 1 1 0 31 43 45 49 31 0 41 49 49 49 36 0 c 14 24 7f 4 0 79 49 49 49 46 0 1e 29 49 49
  //   46 0 61 42 44 48 70 0 36 49 49 49 36 0 31 49 49 4a 3c 0 0 0 22 4*0 1 22 0 0 0 8 14 22 41 0 0 5*14 0
  //   0 41 22 14 8 0 20 40 45 48 30 0 3e 41 5d 4d 38 0 3f 48 48 48 3f 0 7f 49 49 49 36 0 3e 41 41 41 22 0
  //   7f 41 41 22 1c 0 7f 49 49 49 41 0 7f 48 48 40 40 0 3e 41 49 49 4e 0 7f 8 8 8 7f 0 41 41 7f 41 41 0
  //   46 41 41 7e 40 0 7f 8 18 24 43 0 7f 4*1 0 7f 20 10 20 7f 0 7f 20 18 6 7f 0 3e 41 41 41 3e 0 7f 48 48
  //   48 30 0 3e 41 4d 42 3d 0 7f 48 4c 4a 31 0 31 49 49 49 46 0 40 40 7f 40 40 0 7e 1 1 1 7e 0 70 c 3 c
  //   70 0 7e 1 e 1 7e 0 63 14 8 14 63 0 70 8 7 8 70 0 43 45 49 51 61 0 0 0 7f 41 0 0 40 30 8 6 1 0 0 41
  //   7f 0 0 0 10 20 40 20 10 0 5*1 0 0 40 20 0 0 0 4 2a 2a 2a 1c 0 0 7f 9 9 6 0 0 1c 22 22 22 0 0 6 9 9
  //   7f 0 1c 2a 2a 2a 18 0 0 3f 48 48 20 0 0 32 49 49 3e 0 0 3f 4 4 7 5*0 2f 0 0 0 1 1 5e 0 0 7f 8 14 23
  //   0 0 0 3e 1 1 0 f 10 f 10 f 0 1f 8 10 10 f 0 e 11 11 11 e 0 0 1f 24 24 18 0 0 18 24 24 1f 0 0 f 8 8 8
  //   0 0 9 15 15 12 0 0 10 7e 11 11 0 1e 1 1 1 1e 0 1c 2 1 2 1c 0 1e 1 6 1 1e 0 11 a 4 a 11 0 10 8 7 8 10
  //   0 11 13 15 19 11 0 0 0 2a 55 41 5*0 7f 0 0 0 41 5d 2a 0 8 10 8 4 8 0 8 1c 2a 8 8
endmodule

module REGISTROS (
  input  [6:0] DIN,
  input  CLK,
  input  RESET,
  output [6:0] D00,
  output [6:0] D01,
  output [6:0] D02,
  output [6:0] D03,
  output [6:0] D04,
  output [6:0] D05
);

  Register #(.width(7)) register_1 (.D(DIN), .clk(CLK), .Q(D00), .clr(RESET));  // open: en
  Register #(.width(7)) register_2 (.D(D00), .clk(CLK), .Q(D01), .clr(RESET));  // open: en
  Register #(.width(7)) register_3 (.D(D01), .clk(CLK), .Q(D02), .clr(RESET));  // open: en
  Register #(.width(7)) register_4 (.D(D02), .clk(CLK), .Q(D03), .clr(RESET));  // open: en
  Register #(.width(7)) register_5 (.D(D03), .clk(CLK), .Q(D04), .clr(RESET));  // open: en
  Register #(.width(7)) register_6 (.D(D04), .clk(CLK), .Q(D05), .clr(RESET));  // open: en
endmodule

module COLREGISTROS (
  input  [6:0] DIN,
  input  CLK,
  input  RESET,
  output [41:0] D05,
  output [41:0] D11,
  output [41:0] D17,
  output [41:0] D23,
  output [41:0] D29,
  output [41:0] D35,
  output [41:0] D41,
  output [41:0] D47,
  output [41:0] D53,
  output [41:0] D59
);

  REGISTROS registros_1 (
    .DIN(DIN), .CLK(CLK), .RESET(RESET), .D00(D05[6:0]), .D01(D05[13:7]), .D02(D05[20:14]), .D03(D05[27:21]),
    .D04(D05[34:28]), .D05(D05[41:35]));
  REGISTROS registros_2 (
    .DIN(D05[41:35]), .CLK(CLK), .RESET(RESET), .D00(D11[6:0]), .D01(D11[13:7]), .D02(D11[20:14]),
    .D03(D11[27:21]), .D04(D11[34:28]), .D05(D11[41:35]));
  REGISTROS registros_3 (
    .DIN(D11[41:35]), .CLK(CLK), .RESET(RESET), .D00(D17[6:0]), .D01(D17[13:7]), .D02(D17[20:14]),
    .D03(D17[27:21]), .D04(D17[34:28]), .D05(D17[41:35]));
  REGISTROS registros_4 (
    .DIN(D17[41:35]), .CLK(CLK), .RESET(RESET), .D00(D23[6:0]), .D01(D23[13:7]), .D02(D23[20:14]),
    .D03(D23[27:21]), .D04(D23[34:28]), .D05(D23[41:35]));
  REGISTROS registros_5 (
    .DIN(D23[41:35]), .CLK(CLK), .RESET(RESET), .D00(D29[6:0]), .D01(D29[13:7]), .D02(D29[20:14]),
    .D03(D29[27:21]), .D04(D29[34:28]), .D05(D29[41:35]));
  REGISTROS registros_6 (
    .DIN(D29[41:35]), .CLK(CLK), .RESET(RESET), .D00(D35[6:0]), .D01(D35[13:7]), .D02(D35[20:14]),
    .D03(D35[27:21]), .D04(D35[34:28]), .D05(D35[41:35]));
  REGISTROS registros_7 (
    .DIN(D35[41:35]), .CLK(CLK), .RESET(RESET), .D00(D41[6:0]), .D01(D41[13:7]), .D02(D41[20:14]),
    .D03(D41[27:21]), .D04(D41[34:28]), .D05(D41[41:35]));
  REGISTROS registros_8 (
    .DIN(D41[41:35]), .CLK(CLK), .RESET(RESET), .D00(D47[6:0]), .D01(D47[13:7]), .D02(D47[20:14]),
    .D03(D47[27:21]), .D04(D47[34:28]), .D05(D47[41:35]));
  REGISTROS registros_9 (
    .DIN(D47[41:35]), .CLK(CLK), .RESET(RESET), .D00(D53[6:0]), .D01(D53[13:7]), .D02(D53[20:14]),
    .D03(D53[27:21]), .D04(D53[34:28]), .D05(D53[41:35]));
  REGISTROS registros_10 (
    .DIN(D53[41:35]), .CLK(CLK), .RESET(RESET), .D00(D59[6:0]), .D01(D59[13:7]), .D02(D59[20:14]),
    .D03(D59[27:21]), .D04(D59[34:28]), .D05(D59[41:35]));
endmodule

module CONTADOR5 (
  input  CLK,
  input  X,
  input  RESET,
  output [2:0] out_4,
  output Z
);

  wire and_1_out, and_2_out, and_3_out, and_4_out, and_5_out, and_6_out, and_7_out, and_8_out,
       comparator_1_eq, NOQ0, NOQ1, NOQ2, NOX, or_1_out, or_2_out;

  not not_1 (NOX, X);
  and and_1 (and_1_out, NOQ1, out_4[0], X);
  and and_2 (and_2_out, NOQ2, out_4[0], X);
  and and_3 (and_3_out, NOQ2, NOQ0, X);
  or or_1 (or_1_out, and_1_out, and_2_out);
  and and_4 (and_4_out, NOQ2, NOQ1, out_4[0], X);
  and and_5 (and_5_out, NOQ2, out_4[1], out_4[0], X);
  and and_6 (and_6_out, NOQ1, out_4[0], X);
  and and_7 (and_7_out, NOQ1, NOQ0, X);
  or or_2 (or_2_out, and_7_out, and_3_out);
  and and_8 (and_8_out, NOQ2, out_4[1], out_4[0], X);
  S_R_Flip_Flop FF0 (.S(or_2_out), .R(or_1_out), .clk(CLK), .Q(out_4[0]), .reset(RESET), .Qn(NOQ0));  // open: preset
  S_R_Flip_Flop FF1 (.S(and_4_out), .R(and_8_out), .clk(CLK), .Q(out_4[1]), .reset(RESET), .Qn(NOQ1));  // open: preset
  S_R_Flip_Flop FF2 (.S(and_5_out), .R(and_6_out), .clk(CLK), .Q(out_4[2]), .reset(RESET), .Qn(NOQ2));  // open: preset
  D_Flip_Flop d_ff_1 (.D(comparator_1_eq), .clk(CLK), .Q(Z), .reset(RESET));  // open: Qn, preset
  Comparator #(.width(3)) comparator_1 (.a(out_4), .b(3'b101), .eq(comparator_1_eq));  // open: gt, lt

  // Other names for the same wires on the sheet: Q0 = out_4[0]; Q1 = out_4[1]; Q2 = out_4[2]
endmodule

module DIRECCIONROM (
  input  [9:0] DIN,
  input  [2:0] COUNT,
  output [9:0] out_3
);

  wire comparator_1_eq;
  wire [9:0] multiplexer_1_out, multiplier_1_out, subtractor_1_out;

  Comparator #(.width(10)) comparator_1 (.a(DIN), .b({10{1'b0}}), .eq(comparator_1_eq));  // open: gt, lt
  Multiplexer #(.width(10)) multiplexer_1 (.in0(DIN), .in1(10'h20), .out(multiplexer_1_out), .sel(comparator_1_eq));
  Subtractor #(.width(10)) subtractor_1 (.a(multiplexer_1_out), .b(10'h20), .out(subtractor_1_out));  // open: bin, bout
  Multiplier #(.width(10)) multiplier_1 (.a(subtractor_1_out), .b(10'h6), .out(multiplier_1_out));  // open: cin, cout
  Adder #(.width(10)) adder_1 (.a(multiplier_1_out), .b({{7{1'b0}}, COUNT}), .out(out_3));  // open: cin, cout
endmodule

module DIRECCIONRAM (
  input  RESET,
  input  CLK,
  output [6:0] out_3
);

  Counter #(.max('h7f), .width(7)) counter_1 (.clr(RESET), .clk(CLK), .Q(out_3));  // open: load, up, count, D, carry
endmodule
